// Logisim project project2 copy.circ as structural Verilog: 1 circuit, main circuit main
module main (
  output [7:0] RegData1,
  output [7:0] RegData2
);

  wire and_1_out, clock_1_out, Clock_C_out, decoder_1_out0, decoder_1_out1, decoder_1_out2, decoder_1_out3,
       not_1_out, not_2_out, not_3_out;
  wire [7:0] adder_1_out, adder_2_out, Instruction_Memory_data_2, Memory_dout, multiplexer_1_out,
       multiplexer_2_out, PC_q, subtractor_1_out, X0_q, X1_q, X2_q, X3_q;
  wire [17:0] Instruction_Memory_data;

  Clock clock_1 (.out(clock_1_out));
  Register PC (.D(adder_1_out), .en(1'b1), .clk(Clock_C_out), .Q(PC_q));  // open: clr
  RAM Memory (
    .addr(Instruction_Memory_data_2), .oe(Instruction_Memory_data[17]), .clk(clock_1_out), .dout(Memory_dout));  // open: we, din
  ROM #(.dataWidth(18)) Instruction_Memory (
    .addr(PC_q), .data({Instruction_Memory_data[17], Instruction_Memory_data_2, Instruction_Memory_data[8:0]}));
  Adder adder_1 (.a(PC_q), .b(8'h1), .out(adder_1_out));  // open: cin, cout
  Adder adder_2 (.a(RegData1), .b(RegData2), .out(adder_2_out));  // open: cin, cout
  Subtractor subtractor_1 (.a(RegData1), .b(RegData2), .out(subtractor_1_out));  // open: bin, bout
  Clock #(.highDuration(2), .lowDuration(2)) Clock_C (.out(Clock_C_out));
  Multiplexer #(.width(8)) multiplexer_1 (
    .in0(adder_2_out), .in1(subtractor_1_out), .out(multiplexer_1_out), .sel(Instruction_Memory_data[1]));
  not not_1 (not_1_out, Clock_C_out);
  not not_2 (not_2_out, not_1_out);
  Multiplexer #(.width(8)) multiplexer_2 (
    .in0(Memory_dout), .in1(multiplexer_1_out), .out(multiplexer_2_out), .sel(Instruction_Memory_data[0]));
  not not_3 (not_3_out, not_2_out);
  Decoder #(.select(2)) decoder_1 (
    .out0(decoder_1_out0), .out1(decoder_1_out1), .out2(decoder_1_out2), .out3(decoder_1_out3),
    .sel(Instruction_Memory_data[4:3]), .en(Instruction_Memory_data[2]));
  and and_1 (and_1_out, Clock_C_out, not_3_out);
  Register X0 (.D(multiplexer_2_out), .en(decoder_1_out0), .clk(and_1_out), .Q(X0_q));  // open: clr
  Register X1 (.D(multiplexer_2_out), .en(decoder_1_out1), .clk(and_1_out), .Q(X1_q));  // open: clr
  Register X2 (.D(multiplexer_2_out), .en(decoder_1_out2), .clk(and_1_out), .Q(X2_q));  // open: clr
  Register X3 (.D(multiplexer_2_out), .en(decoder_1_out3), .clk(and_1_out), .Q(X3_q));  // open: clr
  Multiplexer #(.select(2), .width(8)) multiplexer_3 (
    .in0(X0_q), .in1(X1_q), .in2(X2_q), .in3(X3_q), .out(RegData1), .sel(Instruction_Memory_data[6:5]));
  Multiplexer #(.select(2), .width(8)) multiplexer_4 (
    .in0(X0_q), .in1(X1_q), .in2(X2_q), .in3(X3_q), .out(RegData2), .sel(Instruction_Memory_data[8:7]));

  // Notes on the sheet:
  //   contents of Instruction_Memory (hex, n*v repeats v):
  //   75 f5 1cf cf 30814 3e00c 24c0c
  //   Data Memory
  //   ALU
  //   ARMADILLOx18
  //   Max Brizzio
  //   Register File
  //   I pledge my honor that I have abided by the Stevens Honor System
endmodule
